# Fritzing sketch granny_synth (saved by Fritzing 0.9.4)
breadboards: 1

parts:
  Raspberry_Pi_1 = Raspberry Pi 3 [part_number=RPI-3-V1.2]  # not connected
  Bauteil1 = LCD1602-I2C
  RE1 = KY-040 Rotary encoder [package=THT]
  RE2 = KY-040 Rotary encoder [package=THT]
  RE3 = KY-040 Rotary encoder [package=THT]
  RE4 = KY-040 Rotary encoder [package=THT]
  RE5 = KY-040 Rotary encoder [package=THT]
  Bauteil2 = Adafruit Pi Cobbler Plus [part_number="Adafruit #2029"]

nets:
  GND: Bauteil1.GND, RE1.GND, RE2.GND, RE3.GND, RE4.GND, RE5.GND, Bauteil2.GND
  VCC: Bauteil1.VCC, Bauteil2.+5V
  N1: Bauteil1.SDA, Bauteil2.SDA
  N2: Bauteil1.SCL, Bauteil2.SCL
  VCC_2: RE1.Vcc, RE2.Vcc, RE3.Vcc, RE4.Vcc, RE5.Vcc, Bauteil2.+3.3V
  N3: RE1.DT, Bauteil2.GPIO17
  N4: RE1.CLK, Bauteil2.GPIO27
  N5: RE2.SW, Bauteil2.GPIO22
  N6: RE2.DT, Bauteil2.GPIO5
  N7: RE2.CLK, Bauteil2.GPIO6
  N8: RE3.SW, Bauteil2.GPIO13
  N9: RE3.DT, Bauteil2.GPIO19
  N10: RE3.CLK, Bauteil2.GPIO26
  N11: RE4.SW, Bauteil2.GPIO18
  N12: RE4.DT, Bauteil2.GPIO23
  N13: RE4.CLK, Bauteil2.GPIO24
  N14: RE5.SW, Bauteil2.GPIO16
  N15: RE5.DT, Bauteil2.GPIO20
  N16: RE5.CLK, Bauteil2.GPIO21

custom parts:
  LCD1602-I2C: A standard character display, usually with 2x16 characters. Comes in many colors with LCM1602 IIC attached.
  KY-040 Rotary encoder: KY-040 Rotary Encoder with switch on breakout borad from AZ Delivery
  Adafruit Pi Cobbler Plus: The Raspberry Pi B+/Pi 2/ Pi 3 has landed on the Maker World like a 40-GPIO pinned, quad-USB ported, credit card sized bomb of DIY joy. And while you can use most of our great Model B accessories by hooking up our downgrade cable, its probably a good time to upgrade your set up and accessorize using all of the Model B+'s / Pi 2's / Pi 3's 40 pins. That's why we now carry the Adafruit Assembled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
